// Logisim project half adder.circ as structural Verilog: 1 circuit, main circuit main
module main (
  input  a,
  input  b,
  output x,
  output y
);

  xor xor_1 (x, a, b);
  and and_1 (y, a, b);
endmodule
